// Logisim project ExeríciosPrimeira Aula.circ as structural Verilog
module ExA (
  input  A,
  input  B,
  input  C,
  input  D,
  input  E,
  input  F,
  input  in_7,
  input  in_8,
  input  in_9,
  input  in_10,
  input  in_11,
  input  in_12,
  output S
);

  wire and_1_out, and_2_out, and_3_out, and_4_out, or_1_out, or_2_out, or_3_out, or_4_out, or_6_out, undriven;

  or or_1 (or_1_out, C, D);
  or or_2 (or_2_out, E, F);
  and and_1 (and_1_out, A, B);
  and and_2 (and_2_out, or_1_out, or_2_out);
  and and_3 (and_3_out, in_7, undriven);
  or or_3 (or_3_out, in_9, in_10);
  or or_4 (or_4_out, in_11, in_12);
  or or_5 (S, and_1_out, and_2_out);
  or or_6 (or_6_out, and_3_out, or_3_out);
  and and_4 (and_4_out, or_6_out, or_4_out);
  LED led_1 ();  // open: in
endmodule

module ExB (
  input  A,
  input  B,
  input  C,
  input  D,
  input  E,
  input  F,
  output S
);

  wire and_1_out;

  and and_1 (and_1_out, A, B, C);
  or or_1 (S, and_1_out, D, E, F);
endmodule

module ExC (
  input  A,
  input  B,
  input  C,
  input  D,
  input  E,
  input  F,
  output S
);

  wire or_1_out;

  or or_1 (or_1_out, A, B, C);
  and and_1 (S, D, E, F, or_1_out);
endmodule

module ExD (
  input  A,
  input  B,
  input  C,
  input  D,
  input  E,
  input  F,
  output S
);

  and and_1 (S, A, B, C, D, E, F);
endmodule
